// Logisim project ReduxV.circ as structural Verilog: 4 circuits, main circuit main
module main (
  output [7:0] out_1,
  output [7:0] out_2
);

  wire and_1_out, button_1_out, clock_1_out;
  wire [7:0] adder_1_out, register_1_q;

  Register register_1 (.D(adder_1_out), .en(1'b1), .clk(clock_1_out), .Q(register_1_q), .clr(button_1_out));
  Adder adder_1 (.a(register_1_q), .b(8'h1), .out(adder_1_out), .cin(1'b0));  // open: cout
  Clock #(.highDuration(2), .lowDuration(2)) clock_1 (.out(clock_1_out));
  Button button_1 (.out(button_1_out));
  and and_1 (and_1_out, out_1[0], out_1[1]);
  dual_port_ram dual_port_ram_1 (
    .addr({8{1'b1}}), .pc(register_1_q), .d(register_1_q), .w(and_1_out), .instr(out_1), .data(out_2));
endmodule

module dual_port_ram (
  input  [7:0] addr,
  input  [7:0] pc,
  input  [7:0] d,
  input  w,
  output [7:0] instr,
  output [7:0] data
);

  wire clock_1_out, or_1_out;
  wire [7:0] multiplexer_1_out;

  Clock clock_1 (.out(clock_1_out));
  or or_1 (or_1_out, w, clock_1_out);
  Multiplexer #(.width(8)) multiplexer_1 (.in0(addr), .in1(pc), .out(multiplexer_1_out), .sel(clock_1_out));
  RAM #(.asyncread("true")) ram_1 (
    .addr(multiplexer_1_out), .we(or_1_out), .oe(1'b1), .clk(clock_1_out), .din(d), .dout(data));
  Register #(.trigger("falling")) pcbuf (.D(data), .en(1'b1), .clk(clock_1_out), .Q(instr));  // open: clr
endmodule

module PC (
  input  [7:0] Constante,
  input  [7:0] d_in,
  input  Load,
  input  Incrementador,
  output [7:0] Saida_PC
);

  wire button_1_out, clock_1_out, or_1_out;
  wire [7:0] adder_1_out, multiplexer_1_out;

  Adder adder_1 (.a(Saida_PC), .b(Constante), .out(adder_1_out));  // open: cin, cout
  Multiplexer #(.width(8)) multiplexer_1 (.in0(adder_1_out), .in1(d_in), .out(multiplexer_1_out), .sel(Load));
  Clock clock_1 (.out(clock_1_out));
  or or_1 (or_1_out, Load, Incrementador);
  Register register_1 (.D(multiplexer_1_out), .en(or_1_out), .clk(clock_1_out), .Q(Saida_PC), .clr(button_1_out));
  Button button_1 (.out(button_1_out));
  Hex_Digit_Display hex_digit_display_1 (.value(Saida_PC[7:4]));  // open: dp
  Hex_Digit_Display hex_digit_display_2 (.value(Saida_PC[3:0]));  // open: dp
endmodule

module Program_Counter (
  input  [7:0] in_1,
  output [7:0] out_2
);

  wire Clock, Reset;

  D_Flip_Flop d_ff_1 (.D(in_1[0]), .clk(Clock), .Q(out_2[0]), .reset(Reset));  // open: Qn, preset
  D_Flip_Flop d_ff_2 (.D(in_1[4]), .clk(Clock), .Q(out_2[4]), .reset(Reset));  // open: Qn, preset
  D_Flip_Flop d_ff_3 (.D(in_1[1]), .clk(Clock), .Q(out_2[1]), .reset(Reset));  // open: Qn, preset
  D_Flip_Flop d_ff_4 (.D(in_1[5]), .clk(Clock), .Q(out_2[5]), .reset(Reset));  // open: Qn, preset
  D_Flip_Flop d_ff_5 (.D(in_1[2]), .clk(Clock), .Q(out_2[2]), .reset(Reset));  // open: Qn, preset
  D_Flip_Flop d_ff_6 (.D(in_1[6]), .clk(Clock), .Q(out_2[6]), .reset(Reset));  // open: Qn, preset
  Clock clock_1 (.out(Clock));
  Button button_1 (.out(Reset));
  D_Flip_Flop d_ff_7 (.D(in_1[3]), .clk(Clock), .Q(out_2[3]), .reset(Reset));  // open: Qn, preset
  D_Flip_Flop d_ff_8 (.D(in_1[7]), .clk(Clock), .Q(out_2[7]), .reset(Reset));  // open: Qn, preset

  // Other names for the same wires on the sheet: E0 = in_1[0]; E1 = in_1[1]; E2 = in_1[2]; E3 = in_1[3]; E4 = in_1[4];
  //   E5 = in_1[5]; E6 = in_1[6]; E7 = in_1[7]; S0 = out_2[0]; S1 = out_2[1]; S2 = out_2[2]; S3 = out_2[3];
  //   S4 = out_2[4]; S5 = out_2[5]; S6 = out_2[6]; S7 = out_2[7]
endmodule
